// Logisim project TLCF.circ as structural Verilog: 1 circuit, main circuit main
module main (
  input  Enable
);

  wire and_1_out, and_2_out, and_3_out, and_4_out, and_5_out, and_6_out, and_7_out, and_8_out, and_9_out,
       and_10_out, and_11_out, and_12_out, and_13_out, and_14_out, clock_1_out, not_1_out, not_2_out,
       not_3_out, not_4_out, not_5_out, not_6_out, not_7_out, not_8_out, not_9_out, not_10_out, not_11_out,
       not_12_out, not_13_out, not_14_out, not_15_out, not_16_out, not_17_out, not_18_out, not_19_out,
       not_20_out, not_21_out, not_22_out, not_23_out, not_24_out, or_1_out, or_2_out, or_3_out, or_4_out,
       or_5_out, or_6_out, or_7_out, or_8_out, t_ff_1_q, t_ff_2_q, t_ff_3_q, t_ff_4_q;

  LED led_1 (.in(or_1_out));
  LED led_2 (.in(and_3_out));
  LED led_3 (.in(or_2_out));
  or or_1 (or_1_out, and_1_out, and_2_out);
  and and_1 (and_1_out, t_ff_4_q, t_ff_3_q, not_1_out);
  and and_2 (and_2_out, t_ff_4_q, t_ff_3_q, not_2_out);
  and and_3 (and_3_out, t_ff_4_q, t_ff_3_q, t_ff_2_q, t_ff_1_q);
  or or_2 (or_2_out, not_3_out, not_4_out);
  not not_1 (not_1_out, t_ff_1_q);
  not not_2 (not_2_out, t_ff_2_q);
  not not_3 (not_3_out, t_ff_4_q);
  not not_4 (not_4_out, t_ff_3_q);
  Clock clock_1 (.out(clock_1_out));
  T_Flip_Flop t_ff_1 (.clk(clock_1_out), .T(Enable), .Q(t_ff_1_q));  // open: Qn, preset, reset, en
  not not_5 (not_5_out, t_ff_4_q);
  not not_6 (not_6_out, t_ff_1_q);
  not not_7 (not_7_out, t_ff_4_q);
  not not_8 (not_8_out, t_ff_2_q);
  not not_9 (not_9_out, t_ff_4_q);
  not not_10 (not_10_out, t_ff_3_q);
  T_Flip_Flop t_ff_2 (.clk(clock_1_out), .T(t_ff_1_q), .Q(t_ff_2_q));  // open: Qn, preset, reset, en
  not not_11 (not_11_out, t_ff_4_q);
  not not_12 (not_12_out, t_ff_3_q);
  not not_13 (not_13_out, t_ff_1_q);
  not not_14 (not_14_out, t_ff_4_q);
  not not_15 (not_15_out, t_ff_3_q);
  not not_16 (not_16_out, t_ff_2_q);
  not not_17 (not_17_out, t_ff_4_q);
  not not_18 (not_18_out, t_ff_3_q);
  and and_4 (and_4_out, not_5_out, t_ff_3_q, not_6_out);
  and and_5 (and_5_out, not_7_out, t_ff_3_q, not_8_out);
  and and_6 (and_6_out, not_9_out, t_ff_3_q, t_ff_2_q, t_ff_1_q);
  or or_3 (or_3_out, t_ff_4_q, not_10_out);
  and and_7 (and_7_out, t_ff_2_q, t_ff_1_q);
  and and_8 (and_8_out, not_11_out, not_12_out, not_13_out);
  and and_9 (and_9_out, not_14_out, not_15_out, not_16_out);
  and and_10 (and_10_out, not_17_out, not_18_out, t_ff_2_q, t_ff_1_q);
  or or_4 (or_4_out, t_ff_4_q, t_ff_3_q);
  or or_5 (or_5_out, and_4_out, and_5_out);
  T_Flip_Flop t_ff_3 (.clk(clock_1_out), .T(and_7_out), .Q(t_ff_3_q));  // open: Qn, preset, reset, en
  LED led_4 (.in(or_5_out));
  LED led_5 (.in(and_6_out));
  LED led_6 (.in(or_3_out));
  or or_6 (or_6_out, and_8_out, and_9_out);
  and and_11 (and_11_out, t_ff_3_q, and_7_out);
  T_Flip_Flop t_ff_4 (.clk(clock_1_out), .T(and_11_out), .Q(t_ff_4_q));  // open: Qn, preset, reset, en
  LED led_7 (.in(or_6_out));
  LED led_8 (.in(and_10_out));
  LED led_9 (.in(or_4_out));
  not not_19 (not_19_out, t_ff_3_q);
  not not_20 (not_20_out, t_ff_1_q);
  not not_21 (not_21_out, t_ff_3_q);
  not not_22 (not_22_out, t_ff_2_q);
  not not_23 (not_23_out, t_ff_3_q);
  not not_24 (not_24_out, t_ff_4_q);
  and and_12 (and_12_out, t_ff_4_q, not_19_out, not_20_out);
  and and_13 (and_13_out, t_ff_4_q, not_21_out, not_22_out);
  and and_14 (and_14_out, t_ff_4_q, not_23_out, t_ff_2_q, t_ff_1_q);
  or or_7 (or_7_out, not_24_out, t_ff_3_q);
  or or_8 (or_8_out, and_12_out, and_13_out);
  LED led_10 (.in(or_8_out));
  LED led_11 (.in(and_14_out));
  LED led_12 (.in(or_7_out));

  // Notes on the sheet:
  //   Green
  //   Yellow
  //   Red
  //   West Signal
  //   4 Way 
  //   Traffic Light Control System
  //   Clock
  //   T3
  //   T2
  //   T1
  //   North Signal
  //   Green
  //   Yellow
  //   Red
  //   T0
  //   South Signal
  //   Green
  //   Yellow
  //   Red
  //   East Signal
  //   Green
  //   Yellow
  //   Red
endmodule
